# Fritzing sketch 2 датчика (saved by Fritzing 0.9.3b)
breadboards: 1

parts:
  Arduino_Nano = Arduino Nano (Rev3.0)
  Датчик_газу = GAS_SENSOR [package=mq-3]
  Part1 = KY-026 Flame Sensor Module [package="Breakout board"]

nets:
  GND: Arduino_Nano.GND, Датчик_газу.GND, Part1.G
  5V: Arduino_Nano.5V, Датчик_газу.VCC, Part1.+
  N1: Arduino_Nano.A1, Датчик_газу.A0
  N2: Arduino_Nano.A0, Part1.A0

custom parts:
  GAS_SENSOR: MQ-3 alcohol gas sensor . FP not tested. SEN-08880.
  KY-026 Flame Sensor Module: KEYES KY-026 Arduino Flame Sensor Module reacts iin the presence of fire.
