# Fritzing sketch Sketch diplom (saved by Fritzing 0.9.3b)
breadboards: 1

parts:
  Модуль_заряду_АКБ = PowerBoost 500 Charger
  Батарея = LIPO-2000mAh [package=lipo-2000]
  Arduino_Nano = Arduino Nano (Rev3.0)
  SIM800L = SIM800L [package=THT]
  п'єзоелемент = Grove Buzz
  DC-DC_перетворювач = RioRand LM2596
  Датчик_вогню = KY-026 Flame Sensor Module [package="Breakout board"]  # not connected
  Датчик_газу = GAS_SENSOR [package=mq-3]  # not connected
  R1 = Resistor [tolerance=±5% resistance=10k package="2512 [SMD]"]
  R2 = Resistor [tolerance=±5% resistance=10k package="2512 [SMD]"]

nets:
  N1: Модуль_заряду_АКБ.GND_BAT_IN, Батарея.-
  N2: Модуль_заряду_АКБ.VBAT_IN, Батарея.+
  GND: Модуль_заряду_АКБ.GND, Arduino_Nano.GND, п'єзоелемент.GND, R2.Pin_0
  N3: Модуль_заряду_АКБ.5.0V, Arduino_Nano.5V
  N4: Arduino_Nano.D2, R1.Pin_0, R2.Pin_1
  N5: Arduino_Nano.D3, SIM800L.SIM_TXD
  N6: Arduino_Nano.D8, п'єзоелемент.SIG
  N7: Arduino_Nano.D9, SIM800L.RST
  N8: SIM800L.5V, DC-DC_перетворювач.Pin_3
  N9: SIM800L.GND, DC-DC_перетворювач.Pin_4
  N10: SIM800L.SIM_RXD, R1.Pin_1

custom parts:
  KY-026 Flame Sensor Module: KEYES KY-026 Arduino Flame Sensor Module reacts iin the presence of fire.
  GAS_SENSOR: MQ-3 alcohol gas sensor . FP not tested. SEN-08880.
